# Fritzing sketch LAN TESTER2 (saved by Fritzing 0.9.5d)

parts:
  LCD1 = 2.8" SPI TFT Module [part_number=MSP2807]
  A1 = wt32-eth01

nets:
  N1: LCD1.pin1, A1.Pin_3
  N2: LCD1.pin2, A1.Pin_2, A1.Pin_11
  N3: LCD1.pin3, A1.Pin_16
  N4: LCD1.pin4, A1.Pin_15
  N5: LCD1.pin5, A1.Pin_20
  N6: LCD1.pin6, A1.Pin_19
  N7: LCD1.pin7, A1.Pin_18
  N8: LCD1.pin8, A1.Pin_12
  N9: LCD1.pin11, A1.Pin_25
  N10: LCD1.pin13, A1.Pin_26
  N11: A1.Pin_13, A1.Pin_17

custom parts:
  2.8" SPI TFT Module: A generic 2.8 inch LCD TFT 320x240 display with touchscreen and SD card slot. Uses the ILI9341 controller, like the Adafruit displays of this size uses.
  wt32-eth01: WT32-ETH01 is an embedded serial port to Ethernet module based on ESP32 series designed by Wireless-Tag.
